# Fritzing sketch circuit (saved by Fritzing 0.9.3b)
breadboards: 1

parts:
  Raspberry_Pi_1 = Raspberry Pi 3 [part_number=RPI-3-V1.2]
  IC1 = IC, DIP package, 16 pins [chip_label=MCP3008]
  R1 = Slide Potentiometer [maximum_resistance=10kΩ]
  M1 = DC Motor
  Part1 = Motor Driver 1A Dual TB6612FNG

nets:
  GND: Raspberry_Pi_1.GND, IC1.pin2, IC1.pin9, IC1.pin14, R1.leg1, Part1.GND
  N1: Raspberry_Pi_1.GIPO17, Part1.PWMA
  N2: Raspberry_Pi_1.GIPO27, Part1.AIN2
  N3: Raspberry_Pi_1.GIPO22, IC1.pin10
  N4: Raspberry_Pi_1.3V3, IC1.pin15, IC1.pin16, R1.leg2
  N5: Raspberry_Pi_1.GIPO10, IC1.pin11
  N6: Raspberry_Pi_1.GIPO9, IC1.pin12
  N7: Raspberry_Pi_1.GIPO11, IC1.pin13
  N8: Raspberry_Pi_1.GIPO23, Part1.STBY
  N9: Raspberry_Pi_1.GIPO18, Part1.AIN1
  5V: Raspberry_Pi_1.5V, Part1.VCC, Part1.VM
  N10: IC1.pin1, R1.wiper
  N11: M1.pin_1, Part1.A02
  N12: M1.pin_2, Part1.A01

notes:
  Slider JST
  ADC power JST
  SPI JST
  Motor power JST ↑
  Motor control JST
  Motor drive JST
  Slider JST ↓
  Motor drive JST  ────⟶
  ↓  ADC power JST
  Motor power JST   ↓
  ⟵───   Motor control JST
  ───────⟶
