# Fritzing sketch circuit (saved by Fritzing 0.9.3b)
breadboards: 1

parts:
  Raspberry_Pi_1 = Raspberry Pi 3 [part_number=RPI-3-V1.2]
  IC1 = IC, DIP package, 16 pins [chip_label=MCP3008]
  R1 = Slide Potentiometer [maximum_resistance=100kΩ]
  M1 = DC Motor  # not connected
  Part1 = Motor Driver 1A Dual TB6612FNG  # not connected

nets:
  N1: Raspberry_Pi_1.GND, IC1.pin2, IC1.pin9
  N2: Raspberry_Pi_1.GIPO22, IC1.pin10
  N3: Raspberry_Pi_1.3V3, IC1.pin15, IC1.pin16, R1.leg2
  N4: Raspberry_Pi_1.GIPO10, IC1.pin11
  N5: Raspberry_Pi_1.GIPO9, IC1.pin12
  N6: Raspberry_Pi_1.GIPO11, IC1.pin13
  N7: IC1.pin1, R1.wiper
